// Logisim project Lab01_Intro.circ as structural Verilog: 1 circuit, main circuit Mux21
module Mux21 (
);


  // Notes on the sheet:
  //   Name
  //   Lab 01: 2-Way, 1-Bit Multiplexer
  //   Date
endmodule
