// Logisim project Lab02_Bool.circ as structural Verilog: 2 circuits, main circuit main
module main (
  input  A1,
  input  B1,
  input  C1
);

  wire equation_1_1_out1;

  LED True1 (.in(equation_1_1_out1));
  Equation_1 equation_1_1 (.In1A(A1), .In1B(B1), .In1C(C1), .Out1(equation_1_1_out1));

  // Notes on the sheet:
  //   Name
  //   Lab 02: Boolean Equations
  //   Date
endmodule

module Equation_1 (
  input  In1A,
  input  In1B,
  input  In1C,
  output Out1
);


  // Notes on the sheet:
  //   (A'BC')+(AB'C')+(ABC)
endmodule
