// Logisim project Lab03_Arithmetic.circ as structural Verilog: 1 circuit, main circuit main
module main (
);


  // Notes on the sheet:
  //   Name
  //   Lab 03: Arithmetic Operations
  //   Date
endmodule
