// Logisim project Lab03_Encoder.circ as structural Verilog: 2 circuits, main circuit main
module main (
  input  In1,
  input  In2,
  input  In3,
  input  In4,
  input  In5,
  input  In6,
  input  In7,
  input  In8,
  input  In9,
  output [3:0] PriOut
);

  Hex_Digit_Display hex_digit_display_1 (.value(PriOut));  // open: dp
  Encoder encoder_1 (
    .In1(In1), .In2(In2), .In3(In3), .In4(In4), .In5(In5), .In6(In6), .In7(In7), .In8(In8), .In9(In9),
    .Out1(PriOut[0]), .Out2(PriOut[1]), .Out3(PriOut[2]), .Out4(PriOut[3]));

  // Notes on the sheet:
  //   Name
  //   Lab 03: Priority Encoder
  //   Date
endmodule

module Encoder (
  input  In1,
  input  In2,
  input  In3,
  input  In4,
  input  In5,
  input  In6,
  input  In7,
  input  In8,
  input  In9,
  output Out1,
  output Out2,
  output Out3,
  output Out4
);
endmodule
