// Logisim project Lab04_Logic.circ as structural Verilog: 1 circuit, main circuit main
module main (
);


  // Notes on the sheet:
  //   Name
  //   Lab 04: Logic Operations
  //   Date
endmodule
