// Logisim project Lab06_PLA.circ as structural Verilog: 4 circuits, main circuit main
module main (
);


  // Notes on the sheet:
  //   George Self
  //   Lab 06: PLA
  //   September 20, 2019
  //   (A'BC)+(ABC'D)+(A'B'CD)
  //   (BCD')+(A'B'C)+(A'BCD')+(ABCD)
endmodule

module Equation_1 (
);


  // Notes on the sheet:
  //   (A'BC')+(AB'C')+(ABC)
endmodule

module Equation_2 (
);


  // Notes on the sheet:
  //   (BCD')+(A'B'C)+(A'BCD')+(ABCD)
endmodule

module Equation_3 (
);


  // Notes on the sheet:
  //   (A'BC')+(AB'C')+(ABC)
  //   (A'B'CD')+(A'BCD)+(AB'CD')+(ABCD')
endmodule
