// Logisim project Lab08_ALU.circ as structural Verilog: 2 circuits, main circuit main
module main (
  input  CI,
  input  [7:0] A,
  input  [7:0] B,
  input  [2:0] Sel,
  input  Mode,
  output CO,
  output Cmp,
  output [7:0] ALU_Out
);

  ALU alu_1 (.CI(CI), .A(A), .B(B), .Sel(Sel), .Mode(Mode), .CO(CO), .Cmp(Cmp), .ALU_Out(ALU_Out));

  // Notes on the sheet:
  //   Name
  //   Lab 08: ALU
  //   Date
  //   Mode
  //   1=Logic
  //   Sel Setting
  //   Arithmetic
  //   0=Arithmetic
  //   0=-1
  //   1=A-1
  //   2=A+B
  //   3=A-B
  //   4=AB-1
  //   5=AB'-1
  //   6=A+A
  //   7=A+1
  //   Logic
  //   0=AB
  //   1=(AB)'
  //   2=A+B
  //   3=(A+B)'
  //   4=A Xor B
  //   5=AB'
  //   6=A+B'
  //   7=A'
endmodule

module ALU (
  input  CI,
  input  [7:0] A,
  input  [7:0] B,
  input  [2:0] Sel,
  input  Mode,
  output CO,
  output Cmp,
  output [7:0] ALU_Out
);
endmodule
