// Logisim project Lab08_React.circ as structural Verilog: 3 circuits, main circuit main
module main (
);

  Button Start ();  // open: out
  Button Stop ();  // open: out
  LED Waiting ();  // open: in

  // Notes on the sheet:
  //   Date
  //   Name
  //   Lab 07: React
endmodule

module Reaction (
  input  start,
  input  stop,
  output Waiting,
  output [3:0] Elapsed10,
  output [3:0] Elapsed01
);


  // Notes on the sheet:
  //   Reaction
endmodule

module Countdown (
  input  Reset,
  output Waiting,
  output Start
);


  // Notes on the sheet:
  //   Countdown
endmodule
