// Logisim project Lab09_ROM.circ as structural Verilog: 2 circuits, main circuit main
module main (
);

  wire magic_8_ball_1_ttyclk, magic_8_ball_1_ttyclr, Reset_out;
  wire [6:0] magic_8_ball_1_ttyout;

  Button Reset (.out(Reset_out));
  Clock sysclk ();  // open: out
  Magic_8_Ball magic_8_ball_1 (
    .rst(Reset_out), .ttyOut(magic_8_ball_1_ttyout), .ttyClk(magic_8_ball_1_ttyclk),
    .ttyClr(magic_8_ball_1_ttyclr));
  TTY tty_1 (.data(magic_8_ball_1_ttyout), .clk(magic_8_ball_1_ttyclk), .clr(magic_8_ball_1_ttyclr));  // open: we

  // Notes on the sheet:
  //   Name
  //   Lab 08: ROM
  //   Date
  //   Tick Freq: 16k
endmodule

module Magic_8_Ball (
  input  rst,
  output [6:0] ttyOut,
  output ttyClk,
  output ttyClr
);

  wire clk, crt, ena, j_k_ff_1_q, j_k_ff_1_qn, load, not_1_out;
  wire [4:0] random_1_out;
  wire [11:0] multiplexer_1_out;

  Random #(.width(5)) random_1 (.clk(ttyClr), .out(random_1_out));  // open: clr, next
  and and_1 (ttyClr, rst, ~ena);  // AND_Gate
  Multiplexer #(.select(5), .width(12), .enable("false")) multiplexer_1 (
    .in0(12'h1), .in1(12'hf), .in2(12'h22), .in3(12'h32), .in4(12'h41), .in5(12'h54), .in6(12'h64),
    .in7(12'h70), .in8(12'h7d), .in9(12'h81), .in10(12'h94), .in11(12'ha9), .in12(12'hb8), .in13(12'hd1),
    .in14(12'he4), .in15(12'hfe), .in16(12'h111), .in17(12'h120), .in18(12'h132), .in19(12'h146),
    .in20(12'h1), .in21(12'hf), .in22(12'h22), .in23(12'h32), .in24(12'h94), .in25(12'ha9), .in26(12'hb8),
    .in27(12'hfe), .in28(12'h111), .in29(12'h120), .in30(12'h132), .in31(12'h146), .out(multiplexer_1_out),
    .sel(random_1_out));
  J_K_Flip_Flop j_k_ff_1 (.J(ttyClr), .K(load), .clk(clk), .Q(j_k_ff_1_q), .Qn(j_k_ff_1_qn));  // open: preset, reset
  J_K_Flip_Flop j_k_ff_2 (.J(j_k_ff_1_q), .K(j_k_ff_1_qn), .clk(not_1_out), .Q(load), .Qn(crt));  // open: preset, reset
  not not_1 (not_1_out, clk);
  Clock #(.highDuration(2), .lowDuration(2)) clock_1 (.out(clk));

  // Notes on the sheet:
  //   Magic 8-Ball
endmodule
