// Logisim project Lab10_RAM.circ as structural Verilog: 1 circuit, main circuit main
module main (
);

  wire clk, rd, rd_wrt_out, Reset_out, wrt;

  T_Flip_Flop t_ff_1 (.T(1'b1), .clk(rd_wrt_out), .Q(wrt), .Qn(rd));  // open: reset, preset
  Button rd_wrt (.out(rd_wrt_out));
  Button u_clk (.out(clk));
  Button Reset (.out(Reset_out));
  RAM ram_1 (.we(wrt), .oe(rd), .clk(clk));  // open: addr, data

  // Notes on the sheet:
  //   Name
  //   Lab 10: RAM
  //   Date
endmodule
