// Logisim project Lab10_Timer.circ as structural Verilog: 4 circuits, main circuit main
module main (
  input  Up_Down,
  input  [7:0] Min,
  input  [7:0] Max,
  output [7:0] OutBin
);

  wire Reset_out;

  Button Reset (.out(Reset_out));
  Timer_V3 timer_v3_1 (.Rst(Reset_out), .Up(Up_Down), .Min(Min), .Max(Max), .OutBin(OutBin));

  // Notes on the sheet:
  //   Name
  //   Lab 06: Timer
  //   Date
endmodule

module Timer_V1 (
  input  Rst,
  input  Load,
  input  CntUp
);

  wire Clk_out, counter_1_carry;
  wire [3:0] binairy_to_bcd_converter_1_p2, binairy_to_bcd_converter_1_p3, binairy_to_bcd_converter_1_p4;
  wire [7:0] counter_1_q;

  Counter #(.ongoal("load")) counter_1 (
    .clr(Rst), .load(Load), .up(CntUp), .clk(Clk_out), .D(8'ha), .carry(counter_1_carry), .Q(counter_1_q));  // open: count
  Button Clk (.out(Clk_out));
  LED Zero (.in(counter_1_carry));
  Hex_Digit_Display hex_digit_display_1 (.value(binairy_to_bcd_converter_1_p2));  // open: dp
  // Binairy_to_BCD_converter #(.binvalue(8)) binairy_to_bcd_converter_1: pin names not known; wires that end beside it: counter_1_q, binairy_to_bcd_converter_1_p2, binairy_to_bcd_converter_1_p3, binairy_to_bcd_converter_1_p4
  Hex_Digit_Display hex_digit_display_2 (.value(binairy_to_bcd_converter_1_p4));  // open: dp
  Hex_Digit_Display hex_digit_display_3 (.value(binairy_to_bcd_converter_1_p3));  // open: dp
endmodule

module Timer_V2 (
  input  Rst,
  input  Up,
  input  [7:0] Max,
  input  [7:0] Min
);

  wire Clk_out, counter_1_carry;
  wire [3:0] binairy_to_bcd_converter_1_p2, binairy_to_bcd_converter_1_p3, binairy_to_bcd_converter_1_p4;
  wire [7:0] counter_1_q, multiplexer_1_out;

  Button Clk (.out(Clk_out));
  Multiplexer #(.width(8), .enable("false")) multiplexer_1 (.in0(Max), .in1(Min), .out(multiplexer_1_out), .sel(Up));
  Counter #(.max('ha), .ongoal("load")) counter_1 (
    .clr(Rst), .up(Up), .clk(Clk_out), .D(multiplexer_1_out), .carry(counter_1_carry), .Q(counter_1_q));  // open: load, count
  LED LoopNext (.in(counter_1_carry));
  Hex_Digit_Display hex_digit_display_1 (.value(binairy_to_bcd_converter_1_p2));  // open: dp
  Hex_Digit_Display hex_digit_display_2 (.value(binairy_to_bcd_converter_1_p3));  // open: dp
  // Binairy_to_BCD_converter #(.binvalue(8)) binairy_to_bcd_converter_1: pin names not known; wires that end beside it: counter_1_q, binairy_to_bcd_converter_1_p2, binairy_to_bcd_converter_1_p3, binairy_to_bcd_converter_1_p4
  Hex_Digit_Display hex_digit_display_3 (.value(binairy_to_bcd_converter_1_p4));  // open: dp
endmodule

module Timer_V3 (
  input  Rst,
  input  Up,
  input  [7:0] Min,
  input  [7:0] Max,
  output [7:0] OutBin
);

  wire clk_out;

  Clock #(.highDuration(2), .lowDuration(2)) clk (.out(clk_out));
  Counter #(.ongoal("load")) counter_1 (.Q(OutBin));  // open: clr, load, up, count, clk, D, carry

  // Notes on the sheet:
  //   Count between min-max
  //   Sel 1 for up and 0 for down
  //   Pulse Rst to reset count
endmodule
