// Logisim project Lab11_Processor.circ as structural Verilog: 4 circuits, main circuit main
module main (
  input  [8:0] mCode
);

  wire clk;

  Button u_clk (.out(clk));
  Control control_1 (.mCode(mCode), .clk(clk));  // open: ALUCtl, RegCtl, dBusCtl
  ALU alu_1 (.clk(clk));  // open: DataIn, ALUCtl, DataOut
  GenReg genreg_1 (.clk(clk));  // open: DataIn, RegSel, DataOut

  // Notes on the sheet:
  //   Name
  //   Lab 11: Processor
  //   Date
endmodule

module ALU (
  input  [7:0] DataIn,
  input  [3:0] ALUCtl,
  input  clk,
  output [7:0] DataOut
);

  wire not_1_out;
  wire [7:0] adder_1_out, adder_2_out, ALUBuffer_q, and_1_out, multiplexer_1_out, negator_1_out, not_2_out,
       or_1_out, xor_1_out;

  Register #(.trigger("falling")) ALUBuffer (.D(DataIn), .en(not_1_out), .clk(clk), .Q(ALUBuffer_q));  // open: clr
  not not_1 (not_1_out, ALUCtl[3]);
  Adder adder_1 (.a(8'h1), .b(DataIn), .out(adder_1_out));  // open: cin, cout
  Adder adder_2 (.a(ALUBuffer_q), .b(DataIn), .out(adder_2_out));  // open: cin, cout
  Negator negator_1 (.in(DataIn), .out(negator_1_out));
  assign and_1_out = ALUBuffer_q & DataIn;  // AND_Gate and_1, 8 bits wide
  assign or_1_out = ALUBuffer_q | DataIn;  // OR_Gate or_1, 8 bits wide
  assign xor_1_out = ALUBuffer_q ^ DataIn;  // XOR_Gate xor_1, 8 bits wide
  assign not_2_out = ~DataIn;  // NOT_Gate not_2, 8 bits wide
  Multiplexer #(.select(3), .width(8), .enable("false")) multiplexer_1 (
    .in0(adder_1_out), .in1(adder_2_out), .in2(negator_1_out), .in3(and_1_out), .in4(or_1_out),
    .in5(xor_1_out), .in6(not_2_out), .in7({8{1'b0}}), .out(multiplexer_1_out), .sel(ALUCtl[2:0]));
  Register #(.trigger("falling")) Acc (.D(multiplexer_1_out), .en(ALUCtl[3]), .clk(clk), .Q(DataOut));  // open: clr

  // Other names for the same wires on the sheet: ALUCtl_t[2:0] = ALUCtl[2:0]; AccEna = ALUCtl[3]

  // Notes on the sheet:
  //   Arithmetic/Logic Unit
  //   Functions
  //   0: Inc dBus
  //   1: Add
  //   2: 2's Comp dBus
  //   3: AND
  //   4: OR
  //   5: XOR
  //   6: NOT dBus
  //   7: Zero
endmodule

module GenReg (
  input  [7:0] DataIn,
  input  [2:0] RegSel,
  input  clk,
  output [7:0] DataOut
);
endmodule

module Control (
  input  [8:0] mCode,
  input  clk,
  output [3:0] ALUCtl,
  output [2:0] RegCtl,
  output [1:0] dBusCtl
);
endmodule
