// Logisim project Lab14_Elevator.circ as structural Verilog: 1 circuit, main circuit main
module main (
);


  // Notes on the sheet:
  //   Name
  //   Lab 12: Elevator
  //   Date
endmodule
